# Fritzing sketch circuit_diagram (saved by Fritzing 0.9.3b)
breadboards: 1

parts:
  Componente1 = Arduino Uno (Rev3)
  S1 = H-Bridge with L298N
  BT1 = Bluetooth HC-06u [package=THT]
  VCC1 = 4 x AAA Battery Mount
  M1 = DC Motor
  M2 = DC Motor
  VCC2 = Battery block 9V

nets:
  N1: Componente1.D9_PWM, S1.IN3
  N2: Componente1.D10_PWM/SS, S1.IN4
  N3: Componente1.D0/RX, BT1.TXD
  N4: Componente1.D1/TX, BT1.RXD
  N5: Componente1.D5_PWM, S1.IN1
  N6: Componente1.D6_PWM, S1.IN2
  5V: Componente1.5V, BT1.VCC
  GND: Componente1.GND, BT1.GND, VCC2.-
  N7: Componente1.VIN, VCC2.+
  N8: S1.12V, VCC1.+
  N9: S1.ENA, S1.ENA-5V
  N10: S1.ENB, S1.ENB-5V
  N11: S1.M1-01, M1.pin_2
  N12: S1.M1-02, M1.pin_1
  N13: S1.M2-01, M2.pin_2
  N14: S1.M2-02, M2.pin_1

custom parts:
  H-Bridge with L298N: h-bridge
  Bluetooth HC-06u: Bluetooth HC-06 - face up, pins down 16.5mm x 37.5mm PCB
